# Fritzing sketch Thermoforming Project (saved by Fritzing 0.9.3b)
stripboards: 5

parts:
  M1 = DOIT Esp32 DevKit v1 (30 pins long, 11 pins width) [part_number=ESP32S-PIN30]
  M2 = RioRand LM2596
  M3 = RioRand LM2596
  A1 = AMS11176 module
  J1 = Camdenboss CTB0158-2 [part_number=CTB0158-2 package=THT]
  J2 = Camdenboss CTB0158-2 [part_number=CTB0158-2 package=THT]
  J3 = Camdenboss CTB0158-2 [part_number=CTB0158-2 package=THT]
  Mod1 = generic-ac-power-supply [package=THT]
  J4 = Camdenboss CTB0158-2 [part_number=CTB0158-2 package=THT]
  PS1 = prefix0000 [part_number=S-350-60]
  J5 = 120V duplex outlet_1

nets:
  3V3: M1.3V3, M1.VIN, M2.Pin_3
  N1: M1.GND, M2.Pin_4, M3.Pin_4, A1.pin3
  N2: M1.D15, M1.D13
  N3: M1.D2, M1.D12
  N4: M1.D4, M1.D14
  N5: M1.RX2, M1.D27
  N6: M1.TX2, M1.D26
  N7: M1.D5, M1.D25, A1.pin2
  N8: M1.D18, M1.D33
  N9: M1.D19, M1.D32
  N10: M1.D21, M1.D35
  N11: M1.RX0, M1.D34
  N12: M1.TX0, M1.VN
  N13: M1.D22, M1.VP
  N14: M1.D23, M1.EN
  N15: M2.Pin_1, J1.pin1, PS1.connector2
  N16: M2.Pin_2, J1.pin2, PS1.connector4
  N17: M3.Pin_1, J2.pin1, Mod1.pin4, J4.pin2
  N18: M3.Pin_2, J2.pin2, Mod1.pin3, J4.pin1
  N19: M3.Pin_3, A1.pin1
  N20: J3.pin1, Mod1.pin1, J5.N1
  N21: J3.pin2, Mod1.pin2, J5.N2

custom parts:
  DOIT Esp32 DevKit v1 (30 pins long, 11 pins width): The DOIT Esp32 DevKit v1 is one of the development board created by DOIT to evaluate the ESP-WROOM-32 module. It is based on the ESP32 microcontroller that boasts Wifi, Bluetooth, Ethernet and Low Power support all in a single chip. (vanepp) made breadboard work, adjusted pin numbering and labels and reduced size of schematic and cleaned up pcb. This chip is 30pins long (2 x15) and 11 pins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
  AMS11176 module: DC-DC step-down modules ( input DC 4.5～7V , output DC 3.3V ).
  generic-ac-power-supply: Generic ac power supply module. Use as is, or customize the svgs to fit your particular device (as they are all different.) Provides AC input and single DC output. This is variant 2, with pcb modified to match the url for a specific device.
  120V duplex outlet_1: 120V duplex outlet.
